# Fritzing sketch Rocket-prototype (saved by Fritzing 0.9.10b)
breadboards: 2

parts:
  J5 = Basic Servo
  J6 = Basic Servo
  J7 = Basic Servo
  J8 = Basic Servo
  A2 = 1x18650 battery shield [package=THT]
  9DOF_Gyro_(I2C) = Adafruit BNO085 9-DOF Orientation IMU Fusion [part_number="Addfruit #4754"]
  Altimeter_(I2C) = MPL3115A2 I2C Barometric Pressure, Altitude, Temperature Sensor
  SD_Module_(SPI) = MicroSD Card Module
  Part10 = Arduino Nano (Rev3.0)
  IRLZ44N = Basic FET N-Channel [package="D2Pak [SMD]"]
  Gate_Pulldown = Resistor [tolerance=±5% resistance=1000 package="0402 [SMD]"]
  Ematch = Resistor [tolerance=±5% resistance=2 package="0402 [SMD]"]
  M1 = cc1101 module  # not connected
  U1 = SUP500F [package=sup500f]  # not connected
  R1 = Resistor [tolerance=±5% resistance=10k package="0805 [SMD]"]
  I2C_Pullups = Resistor [tolerance=±5% resistance=10k package="0805 [SMD]"]

nets:
  GND: J5.gnd, J6.gnd, J7.gnd, J8.gnd, A2.pin_5, A2.pin_8, A2.pin_10, A2.pin_12, 9DOF_Gyro_(I2C).GND, Altimeter_(I2C).GND, SD_Module_(SPI).GND, Part10.GND, IRLZ44N.source, Gate_Pulldown.Pin_1
  VCC: J5.vcc, J6.vcc, J7.vcc, J8.vcc, A2.pin_7, A2.pin_9, A2.pin_11, Part10.VIN, Ematch.Pin_1
  N1: J5.pulse, Part10.D5
  N2: J6.pulse, Part10.D6
  N3: J7.pulse, Part10.D9
  N4: J8.pulse, Part10.D10
  VCC_2: A2.pin_6, 9DOF_Gyro_(I2C).VCC, Altimeter_(I2C).+3V3, SD_Module_(SPI).VCC
  N5: 9DOF_Gyro_(I2C).SDA/MISO/TX, Altimeter_(I2C).SDA, Part10.A4, R1.Pin_1
  N6: 9DOF_Gyro_(I2C).SCL/SCK/RX, Altimeter_(I2C).SCL, Part10.A5, I2C_Pullups.Pin_1
  N7: SD_Module_(SPI).MISO, Part10.D12/MISO
  N8: SD_Module_(SPI).MOSI, Part10.D11/MOSI
  N9: SD_Module_(SPI).SCK, Part10.D13/SCK
  N10: SD_Module_(SPI).CS, Part10.D4
  N11: Part10.5V, R1.Pin_0, I2C_Pullups.Pin_0
  N12: Part10.A1, IRLZ44N.Gate, Gate_Pulldown.Pin_0
  N13: IRLZ44N.drain, Ematch.Pin_0

custom parts:
  1x18650 battery shield: 1x18650 Lithium Battery Shield V3 CC CV Type-C Micro USB Mobile Power Bank DIY Module 5V 3A 3V 1A for iPhone Samsung Xiaomi.
  MPL3115A2 I2C Barometric Pressure, Altitude, Temperature Sensor: This pressure sensor from Freescale is a great low-cost sensing solution for precision measurement of barometric pressure and altitude. The MPL3115A2 has a typical 1.5 Pascal resolution, which can resolve altitude at 0.3 meters (compare to the BMP180 which can do 0.17m). It has some upsides compared to the BMP180, such as interrupt outputs for ultra-low power usage, and its also a heck of a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
  cc1101 module: CC1101 rf module.
