# Fritzing sketch Rocket_final_v1 (saved by Fritzing 0.9.10b)
breadboards: 1
perfboards: 1

parts:
  Mod1 = Raspberry Pi Pico
  BATT1 = LiPoly Battery (1300mAh)
  Part1 = Adafruit BNO085 9-DOF Orientation IMU Fusion [part_number="Addfruit #4754"]
  7_4v_to_5v = RioRand LM2596
  7_4v_to_3_3v = RioRand LM2596
  Part2 = JeePlug experimenter's board
  Gate_Pulldown2 = Resistor [tolerance=±5% resistance=1000 package="0402 [SMD]"]
  Ematch_Motor = Resistor [tolerance=±5% resistance=2 package="0402 [SMD]"]
  IRLZ44N = Basic FET N-Channel [package="D2Pak [SMD]"]
  Part3 = JeePlug experimenter's board
  Gate_Pulldown3 = Resistor [tolerance=±5% resistance=1000 package="0402 [SMD]"]
  Ematch_Parachute = Resistor [tolerance=±5% resistance=2 package="0402 [SMD]"]
  IRLZ44N_2 = Basic FET N-Channel [package="D2Pak [SMD]"]
  Magnetic_connectors = JST-B3P-VH [part_number=JST-B3P-VH package=THT]
  J2 = JST-VHR-3N [part_number=JST-VHR-3N package=THT]
  SERVO1 = Tower Pro SG90 servo [part_number=101246]
  SERVO2 = Tower Pro SG90 servo [part_number=101246]
  SERVO3 = Tower Pro SG90 servo [part_number=101246]
  SERVO4 = Tower Pro SG90 servo [part_number=101246]
  microSD1 = MicroSD Card Module
  Part4 = MPL3115A2 I2C Barometric Pressure, Altitude, Temperature Sensor
  Mod2 = Raspberry Pi Pico
  Part5 = Adafruit BNO085 9-DOF Orientation IMU Fusion [part_number="Addfruit #4754"]
  microSD2 = MicroSD Card Module
  Part6 = MPL3115A2 I2C Barometric Pressure, Altitude, Temperature Sensor
  BATT2 = LiPoly Battery (1300mAh)
  7_4v_to_5v1 = RioRand LM2596
  7_4v_to_3_3v1 = RioRand LM2596
  J3 = Dagu DGServo 9g header connector (female) [package=THT]
  Servo_Connectors = Dagu DGServo 9g header connector (female) [package=THT]
  J5 = Dagu DGServo 9g header connector (female) [package=THT]
  J6 = Dagu DGServo 9g header connector (female) [package=THT]
  SERVO5 = Tower Pro SG90 servo [part_number=101246]  # not connected
  SERVO6 = Tower Pro SG90 servo [part_number=101246]  # not connected
  SERVO7 = Tower Pro SG90 servo [part_number=101246]  # not connected
  SERVO8 = Tower Pro SG90 servo [part_number=101246]  # not connected
  Part7 = JeePlug experimenter's board
  Gate_Pulldown4 = Resistor [tolerance=±5% resistance=1000 package="0402 [SMD]"]
  Ematch_Motor1 = Resistor [tolerance=±5% resistance=2 package="0402 [SMD]"]
  IRLZ44N1 = Basic FET N-Channel [package="D2Pak [SMD]"]
  Part8 = JeePlug experimenter's board
  Gate_Pulldown5 = Resistor [tolerance=±5% resistance=1000 package="0402 [SMD]"]
  Ematch_Parachute1 = Resistor [tolerance=±5% resistance=2 package="0402 [SMD]"]
  IRLZ44N2 = Basic FET N-Channel [package="D2Pak [SMD]"]
  Connectors_(ripped_off_when_launch) = JST-B3P-VH [part_number=JST-B3P-VH package=THT]
  J7 = JST-VHR-3N [part_number=JST-VHR-3N package=THT]
  BAT1 = Battery Holders [package=battery-aa]
  BAT2 = Battery Holders [package=battery-aa]
  BAT3 = Battery Holders [package=battery-aa]
  BAT4 = Battery Holders [package=battery-aa]
  Mod3 = Passive Buzzer

nets:
  GND: Mod1.pin_3, Mod1.pin_8, Mod1.pin_13, Mod1.pin_18, Mod1.pin_23, Mod1.pin_28, Mod1.pin_33, Mod1.pin_38, Mod1.pin_42, Part1.GND, 7_4v_to_5v.Pin_4, 7_4v_to_3_3v.Pin_4, Part2.N$20, Part2.N$31, Part2.N$39, Gate_Pulldown2.Pin_1, IRLZ44N.source, Part3.N$20, Part3.N$31, Part3.N$39, Gate_Pulldown3.Pin_1, IRLZ44N_2.source, Magnetic_connectors.pin3, J2.pin1, J2.pin_4, SERVO1.GND, SERVO2.GND, SERVO3.GND, SERVO4.GND, microSD1.GND, Part4.GND
  N1: Mod1.pin_5, Part1.SCL/SCK/RX
  N2: Mod1.pin_6, Part1.SDA/MISO/TX
  N3: Mod1.pin_14, microSD1.SCK
  N4: Mod1.pin_15, microSD1.MOSI
  N5: Mod1.pin_16, microSD1.MISO
  N6: Mod1.pin_17, microSD1.CS
  N7: Mod1.pin_19, Part4.SDA
  N8: Mod1.pin_20, Part4.SCL
  N9: Mod1.pin_24, Part3.N$16
  N10: Mod1.pin_25, Part2.N$16
  N11: Mod1.pin_26, SERVO4.Signal
  N12: Mod1.pin_27, SERVO3.Signal
  N13: Mod1.pin_31, SERVO2.Signal
  N14: Mod1.pin_32, SERVO1.Signal
  VCC: Mod1.pin_37, Part1.VCC, 7_4v_to_3_3v.Pin_3, microSD1.VCC, Part4.VIN
  N15: BATT1.positive, 7_4v_to_5v.Pin_1, 7_4v_to_3_3v.Pin_1
  N16: BATT1.negative, 7_4v_to_5v.Pin_2, 7_4v_to_3_3v.Pin_2
  +5V: 7_4v_to_5v.Pin_3, Part2.N$41, Ematch_Motor.Pin_0, Part3.N$41, Ematch_Parachute.Pin_0, Magnetic_connectors.pin1, J2.pin_6, SERVO1.+5V, SERVO2.+5V, SERVO3.+5V, SERVO4.+5V
  N17: Part2.N$7, Gate_Pulldown2.Pin_0, IRLZ44N.Gate
  N18: Part2.N$23, Ematch_Motor.Pin_1, IRLZ44N.drain
  N19: Part3.N$7, Gate_Pulldown3.Pin_0, IRLZ44N_2.Gate
  N20: Part3.N$23, Ematch_Parachute.Pin_1, IRLZ44N_2.drain
  GND_2: Mod2.pin_3, Mod2.pin_4, Mod2.pin_8, Mod2.pin_13, Mod2.pin_18, Mod2.pin_23, Mod2.pin_28, Mod2.pin_33, Mod2.pin_38, Mod2.pin_42, Part5.GND, Part5.SDA/MISO/TX, microSD2.GND, Part6.GND, 7_4v_to_5v1.Pin_4, 7_4v_to_3_3v1.Pin_4, J3.gnd, Servo_Connectors.gnd, J5.gnd, J6.gnd, Part8.N$20, Part8.N$31, Part8.N$39, Gate_Pulldown5.Pin_1, IRLZ44N2.source, J7.pin1, J7.pin_4, Mod3.-
  N21: Mod2.pin_5, Part5.SCL/SCK/RX
  N22: Mod2.pin_10, Part6.SCL
  N23: Mod2.pin_11, Part6.SDA
  N24: Mod2.pin_12, Mod3.S
  N25: Mod2.pin_14, microSD2.SCK
  N26: Mod2.pin_15, microSD2.MOSI
  N27: Mod2.pin_16, microSD2.MISO
  N28: Mod2.pin_17, microSD2.CS
  N29: Mod2.pin_24, Part8.N$16
  N30: Mod2.pin_25, J7.pin_6
  N31: Mod2.pin_26, J5.pulse
  N32: Mod2.pin_27, Servo_Connectors.pulse
  N33: Mod2.pin_31, J3.pulse
  N34: Mod2.pin_32, J6.pulse
  VCC_2: Mod2.pin_37, Part5.VCC, microSD2.VCC, Part6.VIN, 7_4v_to_3_3v1.Pin_3, Mod3.NC
  N35: BATT2.positive, 7_4v_to_5v1.Pin_1, 7_4v_to_3_3v1.Pin_1
  N36: BATT2.negative, 7_4v_to_5v1.Pin_2, 7_4v_to_3_3v1.Pin_2
  VCC_3: 7_4v_to_5v1.Pin_3, J3.Vcc, Servo_Connectors.Vcc, J5.Vcc, J6.Vcc, Part8.N$49
  N37: Part7.N$7, Gate_Pulldown4.Pin_0, IRLZ44N1.Gate
  N38: Part7.N$16, Connectors_(ripped_off_when_launch).pin1
  N39: Part7.N$20, Part7.N$31, Part7.N$39, Gate_Pulldown4.Pin_1, IRLZ44N1.source, Connectors_(ripped_off_when_launch).pin3, BAT4.+
  N40: Part7.N$23, Ematch_Motor1.Pin_1, IRLZ44N1.drain
  N41: Part7.N$41, Ematch_Motor1.Pin_0, BAT1.-
  N42: Part8.N$7, Gate_Pulldown5.Pin_0, IRLZ44N2.Gate
  N43: Part8.N$23, Ematch_Parachute1.Pin_1, IRLZ44N2.drain
  N44: Part8.N$41, Ematch_Parachute1.Pin_0
  N45: BAT1.+, BAT2.-
  N46: BAT2.+, BAT3.-
  N47: BAT3.+, BAT4.-

custom parts:
  Raspberry Pi Pico: Raspberry Pi Pico. Based around the RP2040 microcontroller the Pico is a low cost microcontroller device bringing Raspberry Pi quality, cost, and easy of use to the microcontroller space. Jan 2021, Split part in to two versions: tht (this one) and SMD. This one will drill holes for a .1 in header in pcb to allow plugging in the module as well as providing pads to solder the module to the top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
  LiPoly Battery (1300mAh): Lithium Ion Polymer Battery (1300mAh)
  Tower Pro SG90 servo: Original file by John De Cristofaro http://www.adafruit.com/products/1449 Adafruit Feedback Servo (Small) Edited by: e-radionica.com 28/9/2015
  MPL3115A2 I2C Barometric Pressure, Altitude, Temperature Sensor: This pressure sensor from Freescale is a great low-cost sensing solution for precision measurement of barometric pressure and altitude. The MPL3115A2 has a typical 1.5 Pascal resolution, which can resolve altitude at 0.3 meters (compare to the BMP180 which can do 0.17m). It has some upsides compared to the BMP180, such as interrupt outputs for ultra-low power usage, and its also a heck of a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
