# Fritzing sketch silly-goose-0-electronics (saved by Fritzing 0.9.10b)
perfboards: 1

parts:
  Part1 = Arduino Nano (Rev3.0)
  U1 = BATTERY-2 [package=battery-aaa]
  VCC1 = Battery block 9V
  Part2 = InvenSense MPU6050
  Part3 = Barometric Pressure Sensor - BMP180 Breakout (GY-68)
  Part8 = JeePlug experimenter's board
  Gate_Pulldown = Resistor [tolerance=±5% resistance=1000 package="0402 [SMD]"]
  Pyro_Ematch = Resistor [tolerance=±5% resistance=2 package="0402 [SMD]"]
  IRLZ44N2 = Basic FET N-Channel [package="D2Pak [SMD]"]
  microSD1 = MicroSD Card Module
  LED1 = smd LED [color="Red (633nm)" package="1206 [SMD]"]

nets:
  GND: Part1.GND, VCC1.-, Part2.GND, microSD1.GND
  N1: Part1.D11/MOSI, microSD1.MOSI
  N2: Part1.D12/MISO, microSD1.MISO
  N3: Part1.VIN, VCC1.+
  N4: Part1.A7, LED1.anode
  N5: Part1.A5, Part2.SCL, Part3.SCL
  N6: Part1.A4, Part2.SDA, Part3.SDA
  N7: Part1.A0, microSD1.CS
  VCC: Part1.3V3, Part2.VCC, Part3.VCC, microSD1.VCC
  N8: Part1.D13/SCK, microSD1.SCK
  N9: U1.-1, Part8.N$20, Part8.N$31, Part8.N$39, Gate_Pulldown.Pin_1, IRLZ44N2.source
  N10: U1.+1, Part8.N$45, Pyro_Ematch.Pin_0
  N11: Part3.GND, LED1.cathode
  N12: Part8.N$7, Gate_Pulldown.Pin_0, IRLZ44N2.Gate
  N13: Part8.N$23, Pyro_Ematch.Pin_1, IRLZ44N2.drain
